# Fritzing sketch brewflowmeter-breadborad (saved by Fritzing 0.9.1b)

parts:
  Arduino = Arduino Uno (Rev3)
  5v/12v_Relay = Relay [part_number=FRS1B-S package=THT]
  LCD = LCD screen
  R1 = Trimmer Potentiometer [maximum_resistance=10kΩ package=THT]
  Rotary_Encoder = Rotary Encoder [package=THT]
  Solenoid_Valve = Solenoid
  Brass_1/2_flowmeter = Brass 1/2 Flowmeter

nets:
  N1: Arduino.D8, LCD.DB6
  N2: Arduino.D9_PWM, LCD.DB5
  N3: Arduino.D10_PWM/SS, LCD.DB4
  N4: Arduino.D11_PWM/MOSI, LCD.E
  N5: Arduino.D12/MISO, LCD.RS
  GND: Arduino.GND, 5v/12v_Relay.COIL2, LCD.VSS, LCD.R/W, R1.leg1, Rotary_Encoder.EncoderPinA, Brass_1/2_flowmeter.GND
  N6: Arduino.D2, Brass_1/2_flowmeter.Tick
  N7: Arduino.D3_PWM, Rotary_Encoder.EncoderPinC
  N8: Arduino.D4, 5v/12v_Relay.COIL1
  N9: Arduino.D7, LCD.DB7
  5V: Arduino.5V, LCD.VDD, R1.leg2, Rotary_Encoder.EncoderPinB, Brass_1/2_flowmeter.VCC
  N10: 5v/12v_Relay.C1, 5v/12v_Relay.C2, Solenoid_Valve.pin2
  N11: LCD.V0, R1.wiper

custom parts:
  Brass 1/2 Flowmeter: Liquid Flow Meter – Brass 1/2 NPT Threaded. Measure liquid/water flow for your solar, computer cooling, or gardening project using this handy basic flow meter. This sensor sit in line with your water line, and uses a pinwheel sensor to measure how much liquid has moved through it. The pinwheel has a little magnet attached, and there’s a hall effect magnetic sensor on the other side of the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
